# Fritzing sketch laba (saved by Fritzing 0.9.3b)
breadboards: 1

parts:
  Часть1 = Arduino Uno (Rev3)
  AM1 = AM2302 Humidity and Temperature Sensor
  Часть2 = Adafruit DS3231 [part_number="Adafruit #3013"]
  hc-sr1 = hc-sr04
  Часть3 = Adafruit PowerRelay Feather Wing [part_number="Adafruit #3191"]
  LED1 = LEDs [package=led10mm]
  LED2 = LEDs [package=led10mm]
  R1 = PHOTOCELL [package=photocell]
  R2 = Resistor [tolerance=±5% resistance=220 package="0805 [SMD]"]
  R3 = Resistor [tolerance=±5% resistance=220 package="0402 [SMD]"]
  R4 = Resistor [tolerance=±5% resistance=220 package="0402 [SMD]"]
  Часть4 = Soil Moisture Sensor

nets:
  N1: Часть1.A0, Часть4.SIG
  N2: Часть1.A1, R1.P$2, R4.Pin_0
  N3: Часть1.A4/SDA, Часть2.SDA
  N4: Часть1.A5/SCL, Часть2.SCL
  N5: Часть1.D8, hc-sr1.Trig
  N6: Часть1.D9_PWM, hc-sr1.Echo
  N7: Часть1.D12/MISO, LED2.A
  N8: Часть1.D13/SCK, LED1.A
  GND: Часть1.GND, AM1.GND, Часть2.GND, hc-sr1.GND, Часть3.GND, R2.Pin_0, R3.Pin_0, R4.Pin_1, Часть4.GND
  N9: Часть1.D2, AM1.DATA
  N10: Часть1.D7, Часть3.RELAY
  VCC: Часть1.5V, AM1.VDD, Часть2.Vin, hc-sr1.VCC, Часть3.3.3V, R1.P$1, Часть4.VCC
  N11: LED1.C, R3.Pin_1
  N12: LED2.C, R2.Pin_1

custom parts:
  Adafruit DS3231: The datasheet for the DS3231 explains that this part is an "Extremely Accurate I²C-Integrated RTC/TCXO/Crystal". And, hey, it does exactly what it says on the tin! This Real Time Clock (RTC) is the most precise you can get in a small, low power package. Most RTCs use an external 32kHz timing crystal that is used to keep time with low current draw. And that's all well and good, but those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
  Adafruit PowerRelay Feather Wing: A Feather board without ambition is a Feather board without FeatherWings! This is the Power Relay FeatherWing. It gives you power to control, and control over power. Put simply, you can now turn on and off lamps, fans, solenoids, and other small appliances that run on up to 250VAC or DC power using any Feather board. Compared to our smaller Relay FeatherWings, this one can handle a beefy 1200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
